# Fritzing sketch I2C-hookup (saved by Fritzing 0.9.3b)
breadboards: 1

parts:
  U1 = atmega328 [package=dip]
  LED1 = smd LED [color="Red (633nm)" package="1206 [SMD]"]

nets:
  N1: U1.VCC, LED1.anode
  N2: U1.GND#7, LED1.cathode

notes:
  To Bus Pirate 5v
  To Bus Pirate GND
  To Bus Pirate SCK
  To Bus Pirate MOSI
